# Fritzing sketch MinimalDriveboard (saved by Fritzing 0.9.2b)
stripboards: 6

parts:
  Part1 = Arduino Uno (Rev3)
  M1 = Stepper Motor - Unipolar  # not connected
  M2 = Stepper Motor - Bipolar  # not connected
  R1 = Resistor [tolerance=±5% resistance=10k package=THT]
  R2 = Resistor [tolerance=±5% resistance=10k package=THT]
  R3 = Resistor [tolerance=±5% resistance=10k package=THT]
  R4 = Resistor [tolerance=±5% resistance=10k package=THT]
  R7 = Resistor [tolerance=±5% resistance=10k package=THT]
  R8 = Resistor [tolerance=±5% resistance=10k package=THT]
  laser_psu = male pin header, 6 pins [form="♂ (male)"]
  S9 = Pushbutton [package=THT]
  J1 = male pin header, 12 pins [form="♂ (male)"]
  J2 = male pin header, 12 pins [form="♂ (male)"]
  S10 = Reed switch [package=THT]
  S11 = Reed switch [package=THT]
  S12 = Reed switch [package=THT]
  S13 = Reed switch [package=THT]
  S14 = Reed switch [package=THT]
  L1 = Solenoid
  IC1 = IC, DIP package, 4 pins [chip_label=IC]
  R9 = Resistor [tolerance=±5% resistance=360 package=THT]
  D1 = Rectifier Diode [part_number=1N4001 package="300 mil [THT]"]

nets:
  N1: Part1.A0, R1.Pin_0, S10.pin_1
  N2: Part1.A1, R2.Pin_0, S11.pin_1
  N3: Part1.A2, R3.Pin_0, S12.pin_1
  N4: Part1.A3, R4.Pin_0, S13.pin_1
  N5: Part1.D8, J1.pin9
  N6: Part1.D9_PWM, J2.pin9
  N7: Part1.D11_PWM/MOSI, J1.pin8
  N8: Part1.D12/MISO, J2.pin8
  N9: Part1.GND, R1.Pin_1, R2.Pin_1, R3.Pin_1, R4.Pin_1, R7.Pin_0, R8.Pin_0, laser_psu.pin4, laser_psu.pin5, J1.pin10, J2.pin10, IC1.pin2
  N10: Part1.D2, S14.pin_1
  N11: Part1.D3_PWM, S9.leg1
  N12: Part1.D4, R9.Pin_0
  N13: Part1.D6_PWM, laser_psu.pin2
  N14: Part1.5V, laser_psu.pin1, laser_psu.pin6, S9.leg0, S10.pin_2, S11.pin_2, S12.pin_2, S13.pin_2, S14.pin_2
  N15: J1.pin1, J2.pin1, L1.pin1, D1.anode
  N16: J1.pin2, J2.pin2, IC1.pin3
  N17: L1.pin2, IC1.pin4, D1.cathode

notes:
  chiller
  door
  air_assist
  aux2_assist
  aux1_assist
  x-step
  y-step
  z-step
  x-dir
  y-dir
  z-dir
  x1-limit
  x2-limit
  y1-limit
  y2-limit
  z1-limit
  z2-limit
  5V-TH-TL-WP-G-IN
  laser PSU
  GND
  24V
  24V PSU
  x-stepper
  y-stepper
  door-switch
  chiller-interlock
  y-driver
  x-driver
  G201X
  air_assist valve
